# Fritzing sketch LedLamp_sketch (saved by Fritzing 0.9.4)
circuit board: 12.4376cm x 10.4715cm
breadboards: 1

parts:
  Audio_DAC = Pcm5102A module
  Li-ion_battery_(3_7v) = LIPO-2000mAh [package=lipo-2000]
  Ph_10k = PHOTOCELL [package=photocell-kit]
  Sensor = TTP223B Capacitive Touch Sensor Module
  LC = Logic Level Converter [package="Breakout board"]
  PIC = Electrolytic Capacitor [capacitance=4.7mF package="100 mil [THT, electrolytic]"]
  Power_Button = Square Pushbutton
  SBC = Capacitor [package=cap-pth-small2]
  Battery_Connector = XT30PW-M
  Power_input_(F) = XT30PW-F
  Charger = SM5308 battery charger module
  XT30_Male = XT30PW-M
  Power_output_(F) = XT30PW-F
  BT_R2 = Resistor [tolerance=±5% resistance=100k package=THT]
  BT_R1 = Resistor [tolerance=±5% resistance=220k package=THT]
  PH_R_10k = Resistor [tolerance=±5% resistance=10k package=THT]
  ESP32 = ESP32 FIREBEETLE IOT V3 [part_number=ESP32_FIREBEETLE]
  Part1 = Adafruit MAX9814 Electret Microphone Amplifier [part_number="Adafruit #1713"]
  Led1 = WS2812 RGB LED strip
  Led2 = WS2812 RGB LED strip

nets:
  GND: Audio_DAC.Pin_1, Audio_DAC.Pin_5, Ph_10k.P$2, Sensor.GND, LC.L-GND, PIC.-, Power_Button.leg0, SBC.1, Power_output_(F).Pin_1, Power_output_(F).Pin_4, BT_R2.Pin_1, ESP32.GND, ESP32.LIPO-, Part1.GND
  N1: Audio_DAC.Pin_2, ESP32.IO26/D3
  N2: Audio_DAC.Pin_3, ESP32.SCL/IO21
  N3: Audio_DAC.Pin_4, ESP32.IO25/D2
  VCC: Audio_DAC.Pin_6, Sensor.VCC, LC.LV, SBC.2, PH_R_10k.Pin_0, ESP32.3V3, Part1.VDD
  N4: Li-ion_battery_(3_7v).+, Battery_Connector.Pin_3
  N5: Li-ion_battery_(3_7v).-, Battery_Connector.Pin_4
  N6: Ph_10k.P$1, PH_R_10k.Pin_1, ESP32.A0/IO36
  N7: Sensor.SIG, ESP32.IO13/D7
  N8: LC.LV1, ESP32.D0/IO4
  N9: LC.LV2, ESP32.D1/IO16
  N10: LC.H-GND, Power_Button.leg1, Power_input_(F).Pin_2, Power_input_(F).Pin_3, Charger.Pin_1, Charger.Pin_5
  N11: LC.HV, PIC.+, Charger.Pin_4, ESP32.VCC
  N12: LC.HV2, Led2.DIN
  N13: LC.HV1, Led1.GND
  N14: Power_input_(F).Pin_1, Power_input_(F).Pin_4, Charger.Pin_2, Power_output_(F).Pin_3, BT_R1.Pin_0
  N15: XT30_Male.Pin_3, Led1.DIN, Led2.GND
  VCC_2: XT30_Male.Pin_4, Led1.VCC, Led2.VCC
  N16: BT_R2.Pin_0, BT_R1.Pin_1, ESP32.A1/IO39
  N17: ESP32.A3/IO35, Part1.OUTPUT

custom parts:
  Pcm5102A module: Interface I2S PCM5102A DAC Decoder GY-PCM5102 I2S Player Module for Raspberry Pi pHAT Format Board Digital PCM5102 Audio Board.
  TTP223B Capacitive Touch Sensor Module: The TTP223B capacitive touch sensor module uses the TTP223B IC. The appropriate voltage is approximately 2 to 5.5 volts.
  Logic Level Converter: 5V to/from 3.3V logic level converter
  XT30PW-M: Connector: DC supply; socket; male; XT30; 15A; 500V; PIN: 2; THT.
  XT30PW-F: Connector: DC supply; socket; female; XT30; 15A; 500V; PIN: 2; THT.
  SM5308 battery charger module: Charger module for Lipo Battery from Usb, 5v 2a, Sm5308 chip.
  ESP32 FIREBEETLE IOT V3: DFRobot Firebeetle ESP32 IOT Microcontroller V3, 36-Pin ESP32.
  Adafruit MAX9814 Electret Microphone Amplifier: Add an ear to your project with this well-designed electret microphone amplifier with AGC. This fully assembled and tested board comes with a 20-20KHz electret microphone soldered on. For the amplification, we use the Maxim MAX9814, a specialty chip that is designed for amplifying electret microphones in situations where the loudness of the audio isn't predictable. This fancy microphone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
  WS2812 RGB LED strip: WS2812 strip
